// Logisim project control-logic.circ as structural Verilog: 1 circuit, main circuit control_logic
module control_logic (
  input  [31:0] inst,
  input  BrEq,
  input  BrLt,
  output PCSel,
  output RegWEn,
  output [2:0] ImmSel,
  output BrUn,
  output ASel,
  output BSel,
  output [3:0] ALUSel,
  output MemRW,
  output [1:0] WBSel,
  output CSRSel,
  output CSRWen
);

  wire and_1_out, and_2_out, and_3_out, and_4_out, and_5_out, and_6_out, and_7_out, and_8_out, and_9_out,
       and_10_out, and_11_out, and_12_out, and_13_out, and_14_out, and_15_out, and_16_out, and_17_out,
       and_18_out, and_19_out, and_20_out, and_21_out, and_22_out, and_23_out, and_24_out, and_25_out,
       and_26_out, and_27_out, and_28_out, and_29_out, comparator_11_eq, IS_CSRW, IS_I_TYPE_0, IS_I_TYPE_1,
       IS_IJUMP_TYPE_0, IS_R_TYPE_0, IS_S_TYPE_0, IS_SB_TYPE_0, IS_U_TYPE_0, IS_U_TYPE_1, IS_UJ_TYPE_0,
       not_1_out, not_2_out, or_1_out, priority_encoder_1_gs, priority_encoder_2_gs, priority_encoder_3_gs,
       priority_encoder_4_gs, priority_encoder_5_gs, priority_encoder_6_gs, xor_1_out, xor_2_out;
  wire [4:0] adder_1_out, adder_2_out, adder_3_out, adder_5_out, priority_encoder_1_out,
       priority_encoder_2_out, priority_encoder_3_out, priority_encoder_4_out, priority_encoder_5_out,
       priority_encoder_6_out, priority_encoder_7_out, priority_encoder_8_out, priority_encoder_9_out,
       priority_encoder_10_out, priority_encoder_11_out, priority_encoder_12_out;
  wire [5:0] adder_4_out, adder_6_out, bit_extender_1_out, bit_extender_2_out, bit_extender_3_out,
       bit_extender_4_out, multiplexer_2_out, multiplexer_3_out, multiplexer_4_out, multiplexer_5_out,
       multiplexer_6_out, TO_ROM, undriven;

  ROM #(.addrWidth(6), .dataWidth(16)) rom_1 (
    .addr(TO_ROM), .data({RegWEn, ImmSel, BrUn, ASel, BSel, ALUSel, MemRW, WBSel, CSRSel, CSRWen}));
  Comparator #(.mode("unsigned"), .width(7)) comparator_1 (
    .a(inst[6:0]), .b(7'b0010011), .eq(IS_I_TYPE_1));  // open: gt, lt
  Comparator #(.mode("unsigned"), .width(7)) comparator_2 (
    .a(inst[6:0]), .b(7'b0000011), .eq(IS_I_TYPE_0));  // open: gt, lt
  Comparator #(.mode("unsigned"), .width(7)) comparator_3 (
    .a(inst[6:0]), .b(7'b0110011), .eq(IS_R_TYPE_0));  // open: gt, lt
  Comparator #(.mode("unsigned"), .width(7)) comparator_4 (
    .a(inst[6:0]), .b(7'b1100011), .eq(IS_SB_TYPE_0));  // open: gt, lt
  Comparator #(.mode("unsigned"), .width(7)) comparator_5 (
    .a(inst[6:0]), .b(7'b0100011), .eq(IS_S_TYPE_0));  // open: gt, lt
  Comparator #(.mode("unsigned"), .width(7)) comparator_6 (
    .a(inst[6:0]), .b(7'b0010111), .eq(IS_U_TYPE_0));  // open: gt, lt
  Comparator #(.mode("unsigned"), .width(7)) comparator_7 (
    .a(inst[6:0]), .b(7'b0110111), .eq(IS_U_TYPE_1));  // open: gt, lt
  Comparator #(.mode("unsigned"), .width(7)) comparator_8 (
    .a(inst[6:0]), .b(7'b1101111), .eq(IS_UJ_TYPE_0));  // open: gt, lt
  Comparator #(.mode("unsigned"), .width(7)) comparator_9 (
    .a(inst[6:0]), .b(7'b1100111), .eq(IS_IJUMP_TYPE_0));  // open: gt, lt
  Comparator #(.mode("unsigned"), .width(7)) comparator_10 (
    .a(inst[6:0]), .b(7'b1110011), .eq(IS_CSRW));  // open: gt, lt
  Priority_Encoder #(.select(5)) priority_encoder_1 (
    .in12(IS_I_TYPE_0), .in15(IS_I_TYPE_1), .out(priority_encoder_1_out), .gs(priority_encoder_1_gs));  // open: in0, in1, in2, in3, in4, in5, in6, in7, in8, in9, in10, in11, in13, in14, in16, in17, in18, in19, in20, in21, in22, in23, in24, in25, in26, in27, in28, in29, in30, in31, en_out, en_in
  and and_1 (and_1_out, inst[13], inst[14]);
  and and_2 (and_2_out, inst[12], inst[14]);
  not not_1 (not_1_out, inst[12]);
  and and_3 (and_3_out, ~inst[2], ~inst[4]);  // AND_Gate
  and and_4 (and_4_out, inst[12], inst[14]);
  and and_5 (and_5_out, and_2_out, ~inst[13]);  // AND_Gate
  Comparator #(.mode("unsigned"), .width(7)) comparator_11 (
    .a(7'b0100000), .b(inst[31:25]), .eq(comparator_11_eq));  // open: gt, lt
  Priority_Encoder #(.select(5)) priority_encoder_2 (
    .in0(IS_R_TYPE_0), .out(priority_encoder_2_out), .gs(priority_encoder_2_gs));  // open: in1, in2, in3, in4, in5, in6, in7, in8, in9, in10, in11, in12, in13, in14, in15, in16, in17, in18, in19, in20, in21, in22, in23, in24, in25, in26, in27, in28, in29, in30, in31, en_out, en_in
  Priority_Encoder #(.select(5)) priority_encoder_3 (
    .in23(IS_S_TYPE_0), .out(priority_encoder_3_out), .gs(priority_encoder_3_gs));  // open: in0, in1, in2, in3, in4, in5, in6, in7, in8, in9, in10, in11, in12, in13, in14, in15, in16, in17, in18, in19, in20, in21, in22, in24, in25, in26, in27, in28, in29, in30, in31, en_out, en_in
  Priority_Encoder #(.select(5)) priority_encoder_4 (
    .in28(IS_IJUMP_TYPE_0), .in29(IS_UJ_TYPE_0), .in30(IS_U_TYPE_1), .in31(IS_U_TYPE_0),
    .out(priority_encoder_4_out), .gs(priority_encoder_4_gs));  // open: in0, in1, in2, in3, in4, in5, in6, in7, in8, in9, in10, in11, in12, in13, in14, in15, in16, in17, in18, in19, in20, in21, in22, in23, in24, in25, in26, in27, en_out, en_in
  Priority_Encoder #(.select(5)) priority_encoder_5 (
    .in31(IS_CSRW), .out(priority_encoder_5_out), .gs(priority_encoder_5_gs));  // open: in0, in1, in2, in3, in4, in5, in6, in7, in8, in9, in10, in11, in12, in13, in14, in15, in16, in17, in18, in19, in20, in21, in22, in23, in24, in25, in26, in27, in28, in29, in30, en_out, en_in
  xor xor_1 (xor_1_out, BrEq, inst[12]);
  xor xor_2 (xor_2_out, inst[12], BrLt);
  and and_6 (and_6_out, and_3_out, inst[6]);
  not not_2 (not_2_out, inst[12]);
  and and_7 (and_7_out, and_5_out, comparator_11_eq);
  and and_8 (and_8_out, inst[25], inst[12]);
  and and_9 (and_9_out, inst[12], inst[13]);
  and and_10 (and_10_out, inst[13], ~inst[14]);  // AND_Gate
  and and_11 (and_11_out, inst[12], inst[14]);
  and and_12 (and_12_out, inst[13], inst[14]);
  Priority_Encoder #(.select(5)) priority_encoder_6 (
    .in26(IS_SB_TYPE_0), .out(priority_encoder_6_out), .gs(priority_encoder_6_gs));  // open: in0, in1, in2, in3, in4, in5, in6, in7, in8, in9, in10, in11, in12, in13, in14, in15, in16, in17, in18, in19, in20, in21, in22, in23, in24, in25, in27, in28, in29, in30, in31, en_out, en_in
  and and_13 (and_13_out, ~inst[12], ~inst[13]);  // AND_Gate
  and and_14 (and_14_out, ~inst[12], ~inst[13]);  // AND_Gate
  and and_15 (and_15_out, inst[12], inst[14]);
  and and_16 (and_16_out, xor_1_out, ~inst[14]);  // AND_Gate
  and and_17 (and_17_out, xor_2_out, inst[14]);
  and and_18 (and_18_out, and_10_out, ~inst[12]);  // AND_Gate
  and and_19 (and_19_out, and_13_out, ~inst[14]);  // AND_Gate
  and and_20 (and_20_out, inst[12], inst[14]);
  and and_21 (and_21_out, inst[13], inst[14]);
  and and_22 (and_22_out, inst[12], inst[13]);
  and and_23 (and_23_out, and_14_out, ~inst[14]);  // AND_Gate
  assign bit_extender_1_out = {{1{1'b0}}, priority_encoder_4_out};  // Bit_Extender bit_extender_1
  assign bit_extender_2_out = {{1{1'b0}}, priority_encoder_9_out};  // Bit_Extender bit_extender_2
  assign bit_extender_3_out = {{1{1'b0}}, priority_encoder_5_out};  // Bit_Extender bit_extender_3
  assign bit_extender_4_out = {{1{1'b0}}, priority_encoder_7_out};  // Bit_Extender bit_extender_4
  or or_1 (or_1_out, and_16_out, and_17_out);
  Adder #(.width(5)) adder_1 (
    .a(priority_encoder_1_out), .b(priority_encoder_8_out), .out(adder_1_out));  // open: cin, cout
  and and_24 (and_24_out, and_4_out, and_1_out);
  Adder #(.width(5)) adder_2 (
    .a(priority_encoder_2_out), .b(priority_encoder_11_out), .out(adder_2_out));  // open: cin, cout
  and and_25 (and_25_out, and_11_out, inst[30]);
  and and_26 (and_26_out, and_22_out, inst[14]);
  Adder #(.width(5)) adder_3 (
    .a(priority_encoder_3_out), .b(priority_encoder_10_out), .out(adder_3_out));  // open: cin, cout
  Adder #(.width(6)) adder_4 (.a(bit_extender_3_out), .b(bit_extender_4_out), .out(adder_4_out));  // open: cin, cout
  Priority_Encoder #(.select(5)) priority_encoder_7 (
    .in5(inst[12]), .in6(and_15_out), .out(priority_encoder_7_out));  // open: in0, in1, in2, in3, in4, in7, in8, in9, in10, in11, in12, in13, in14, in15, in16, in17, in18, in19, in20, in21, in22, in23, in24, in25, in26, in27, in28, in29, in30, in31, gs, en_out, en_in
  and and_27 (and_27_out, or_1_out, and_6_out);
  and and_28 (and_28_out, inst[6], inst[2]);
  Priority_Encoder #(.select(5)) priority_encoder_8 (
    .in0(not_2_out), .in1(inst[12]), .in2(inst[13]), .in3(inst[14]), .in4(and_4_out), .in5(and_7_out),
    .in6(and_1_out), .in7(and_24_out), .out(priority_encoder_8_out));  // open: in8, in9, in10, in11, in12, in13, in14, in15, in16, in17, in18, in19, in20, in21, in22, in23, in24, in25, in26, in27, in28, in29, in30, in31, gs, en_out, en_in
  Adder #(.width(5)) adder_5 (
    .a(priority_encoder_6_out), .b(priority_encoder_12_out), .out(adder_5_out));  // open: cin, cout
  Adder #(.width(6)) adder_6 (.a(bit_extender_1_out), .b(bit_extender_2_out), .out(adder_6_out));  // open: cin, cout
  Priority_Encoder #(.select(5)) priority_encoder_9 (
    .in1(IS_U_TYPE_0), .in3(IS_U_TYPE_1), .in5(IS_UJ_TYPE_0), .in7(IS_IJUMP_TYPE_0),
    .out(priority_encoder_9_out));  // open: in0, in2, in4, in6, in8, in9, in10, in11, in12, in13, in14, in15, in16, in17, in18, in19, in20, in21, in22, in23, in24, in25, in26, in27, in28, in29, in30, in31, gs, en_out, en_in
  or or_2 (PCSel, and_27_out, and_28_out);
  Multiplexer #(.enable("false"), .width(6)) multiplexer_1 (
    .in0(multiplexer_2_out), .in1({1'b0, adder_1_out}), .out(TO_ROM), .sel(priority_encoder_1_gs));
  Multiplexer #(.enable("false"), .width(6)) multiplexer_2 (
    .in0(multiplexer_6_out), .in1({1'b0, adder_2_out}), .out(multiplexer_2_out), .sel(priority_encoder_2_gs));
  and and_29 (and_29_out, inst[12], and_12_out);
  Multiplexer #(.enable("false"), .width(6)) multiplexer_3 (
    .in0(multiplexer_4_out), .in1({1'b0, adder_3_out}), .out(multiplexer_3_out), .sel(priority_encoder_3_gs));
  Priority_Encoder #(.select(5)) priority_encoder_10 (
    .in0(and_23_out), .in1(inst[12]), .in2(inst[13]), .out(priority_encoder_10_out));  // open: in3, in4, in5, in6, in7, in8, in9, in10, in11, in12, in13, in14, in15, in16, in17, in18, in19, in20, in21, in22, in23, in24, in25, in26, in27, in28, in29, in30, in31, gs, en_out, en_in
  Multiplexer #(.enable("false"), .width(6)) multiplexer_4 (
    .in0(multiplexer_5_out), .in1(adder_6_out), .out(multiplexer_4_out), .sel(priority_encoder_4_gs));
  Multiplexer #(.enable("false"), .width(6)) multiplexer_5 (
    .in0(undriven), .in1(adder_4_out), .out(multiplexer_5_out), .sel(priority_encoder_5_gs));
  Priority_Encoder #(.select(5)) priority_encoder_11 (
    .in0(not_1_out), .in1(inst[25]), .in2(inst[30]), .in3(inst[12]), .in4(and_8_out), .in5(and_9_out),
    .in6(and_18_out), .in7(inst[14]), .in8(and_11_out), .in9(and_25_out), .in10(and_12_out),
    .in11(and_29_out), .out(priority_encoder_11_out));  // open: in12, in13, in14, in15, in16, in17, in18, in19, in20, in21, in22, in23, in24, in25, in26, in27, in28, in29, in30, in31, gs, en_out, en_in
  Multiplexer #(.enable("false"), .width(6)) multiplexer_6 (
    .in0(multiplexer_3_out), .in1({1'b0, adder_5_out}), .out(multiplexer_6_out), .sel(priority_encoder_6_gs));
  Priority_Encoder #(.select(5)) priority_encoder_12 (
    .in0(and_19_out), .in1(inst[12]), .in2(inst[14]), .in3(and_20_out), .in4(and_21_out), .in5(and_26_out),
    .out(priority_encoder_12_out));  // open: in6, in7, in8, in9, in10, in11, in12, in13, in14, in15, in16, in17, in18, in19, in20, in21, in22, in23, in24, in25, in26, in27, in28, in29, in30, in31, gs, en_out, en_in

  // Other names for the same wires on the sheet: opcode[6:0] = inst[6:0]; funct3[2:0] = inst[14:12]

  // Notes on the sheet:
  //   INPUTS to your circuit
  //   Break apart instruction and match to type
  //   Connect ROM Input here ->
  //   contents of rom_1 (hex, n*v repeats v):
  //   9004 9104 9184 9024 9124 9164 9044 9084 90a4 91a4 90c4 90e4 9208 9208 9208 9204 9224 9244 9284 92a4
  //   93a4 92c4 92e4 2214 2214 2218 4*3604 3e04 3e04 c604 c3e4 d600 9200 6005 6207
  //   ROM FOR CONTROL LOGIC
  //   DON'T CHANGE THE LOCATIONS OF THE INPUTS AND OUTPUTS!
  //   OUTPUT from your circuit
  //   CLOSE
  //   WIRE
  //   TO
  //   USE
  //   Match Oppcode to type (FOR I)
  //   Spit out number for opcode for I
  //   Spit out number for opcode for S TYPE
  //   Spit out number for opcode for U TYPE
  //   Spit out number for opcode for CSRW TYPE
  //   Reminder: Use combinational logic for PCSel
  //   Spit out number for opcode for R
  //   Spit out number for opcode for SB TYPE
  //   Spit out number for func 3
  //   Spit out number for func 3
  //   Spit out number for func 3
  //   Spit out number for func 3
  //   Spit out number for func 3
endmodule
