// Logisim project cpu.circ as structural Verilog: 1 circuit, main circuit cpu
module cpu (
  input  clk,
  input  [31:0] INSTRUCTION,
  input  [31:0] MEM_READ_DATA,
  output [31:0] MEM_WRITE_ADDRESS,
  output [31:0] PROGRAM_COUNTER,
  output [31:0] ra,
  output [31:0] sp,
  output [31:0] t0,
  output [31:0] t1,
  output [31:0] t2,
  output [31:0] s0,
  output [31:0] s1,
  output [31:0] a0,
  output [31:0] tohost,
  output [3:0] MEM_WRITE_ENABLE,
  output [31:0] MEM_WRITE_DATA
);

  wire and_1_out, and_2_out, and_3_out, and_4_out, and_5_out, and_6_out, and_7_out, ASel, BeEq, BrLt, BrUn,
       BSel, comparator_1_eq, comparator_2_eq, comparator_3_eq, comparator_4_eq, comparator_5_eq,
       control_logic_1_csrsel, control_logic_1_csrwen, memRw, RegWEn, tehPcSel;
  wire [1:0] priority_encoder_4_out, WB_SEL;
  wire [2:0] ImmSel;
  wire [3:0] ALU_SEL_CPU, multiplexer_6_out, priority_encoder_1_out, priority_encoder_2_out,
       priority_encoder_3_out;
  wire [31:0] bit_extender_1_out, bit_extender_2_out, bit_extender_3_out, bit_extender_4_out,
       bit_extender_5_out, bit_extender_6_out, DATA_FROM_READ_DATA_2, DATA_TO_READ, imm_gen_1_imm,
       multiplexer_1_out, multiplexer_2_out, multiplexer_3_out, multiplexer_4_out, multiplexer_5_out,
       multiplexer_8_out, pcPlus4, regfile_1_read_data_1;

  Adder #(.width(32)) adder_1 (.a(PROGRAM_COUNTER), .b(32'h4), .out(pcPlus4));  // open: cin, cout
  Multiplexer #(.enable("false"), .width(32)) multiplexer_1 (
    .in0(pcPlus4), .in1(MEM_WRITE_ADDRESS), .out(multiplexer_1_out), .sel(tehPcSel));
  Register #(.width(32)) PC (.D(multiplexer_1_out), .clk(clk), .Q(PROGRAM_COUNTER));  // open: en, clr
  control_logic control_logic_1 (
    .CSRWen(control_logic_1_csrwen), .PCSel(tehPcSel), .RegWEn(RegWEn), .ImmSel(ImmSel), .BrUn(BrUn),
    .ASel(ASel), .BSel(BSel), .ALUSel(ALU_SEL_CPU), .MemRW(memRw), .WBSel(WB_SEL),
    .CSRSel(control_logic_1_csrsel), .inst(INSTRUCTION), .BrEq(BeEq), .BrLt(BrLt));
  regfile regfile_1 (
    .rs1(INSTRUCTION[19:15]), .rs2(INSTRUCTION[24:20]), .rd(INSTRUCTION[11:7]),
    .Write_Data(multiplexer_5_out), .RegWEn(RegWEn), .clk(clk), .ra(ra), .sp(sp), .t0(t0), .t1(t1), .t2(t2),
    .s0(s0), .s1(s1), .a0(a0), .Read_Data_1(regfile_1_read_data_1), .Read_Data_2(DATA_FROM_READ_DATA_2));
  imm_gen imm_gen_1 (.inst(INSTRUCTION), .ImmSel(ImmSel), .imm(imm_gen_1_imm));
  branch_comp branch_comp_1 (
    .rs1(regfile_1_read_data_1), .rs2(DATA_FROM_READ_DATA_2), .BrUn(BrUn), .BrEq(BeEq), .BrLt(BrLt));
  Multiplexer #(.enable("false"), .width(32)) multiplexer_2 (
    .in0(regfile_1_read_data_1), .in1(PROGRAM_COUNTER), .out(multiplexer_2_out), .sel(ASel));
  Multiplexer #(.enable("false"), .width(32)) multiplexer_3 (
    .in0(DATA_FROM_READ_DATA_2), .in1(imm_gen_1_imm), .out(multiplexer_3_out), .sel(BSel));
  Multiplexer #(.enable("false"), .width(32)) multiplexer_4 (
    .in0(multiplexer_2_out), .in1(multiplexer_3_out), .out(multiplexer_4_out), .sel(control_logic_1_csrsel));
  alu alu_1 (.Result(MEM_WRITE_ADDRESS), .A(multiplexer_2_out), .B(multiplexer_3_out), .ALUSel(ALU_SEL_CPU));
  Multiplexer #(.enable("false"), .select(2), .width(32)) multiplexer_5 (
    .in0(pcPlus4), .in1(MEM_WRITE_ADDRESS), .in2(DATA_TO_READ), .out(multiplexer_5_out), .sel(WB_SEL));  // open: in3
  // csr csr_1: pin names not known; wires that end beside it: INSTRUCTION[31:20], multiplexer_4_out, control_logic_1_csrwen, clk, tohost
  and and_1 (and_1_out, ~MEM_WRITE_ADDRESS[0], ~MEM_WRITE_ADDRESS[1]);  // AND_Gate
  and and_2 (and_2_out, MEM_WRITE_ADDRESS[0], ~MEM_WRITE_ADDRESS[1]);  // AND_Gate
  and and_3 (and_3_out, ~MEM_WRITE_ADDRESS[0], MEM_WRITE_ADDRESS[1]);  // AND_Gate
  and and_4 (and_4_out, MEM_WRITE_ADDRESS[0], MEM_WRITE_ADDRESS[1]);
  and and_5 (and_5_out, ~MEM_WRITE_ADDRESS[0], ~MEM_WRITE_ADDRESS[1]);  // AND_Gate
  and and_6 (and_6_out, ~MEM_WRITE_ADDRESS[0], MEM_WRITE_ADDRESS[1]);  // AND_Gate
  Priority_Encoder #(.select(4)) priority_encoder_1 (
    .in1(and_1_out), .in2(and_2_out), .in4(and_3_out), .in8(and_4_out), .out(priority_encoder_1_out));  // open: in0, in3, in5, in6, in7, in9, in10, in11, in12, in13, in14, in15, gs, en_out, en_in
  Priority_Encoder #(.select(4)) priority_encoder_2 (
    .in3(and_5_out), .in12(and_6_out), .out(priority_encoder_2_out));  // open: in0, in1, in2, in4, in5, in6, in7, in8, in9, in10, in11, in13, in14, in15, gs, en_out, en_in
  Priority_Encoder #(.select(4)) priority_encoder_3 (
    .in15(1'b1), .out(priority_encoder_3_out));  // open: in0, in1, in2, in3, in4, in5, in6, in7, in8, in9, in10, in11, in12, in13, in14, gs, en_out, en_in
  Comparator #(.width(3)) comparator_1 (.a(3'b000), .b(INSTRUCTION[14:12]), .eq(comparator_1_eq));  // open: gt, lt
  Comparator #(.width(3)) comparator_2 (.a(3'b001), .b(INSTRUCTION[14:12]), .eq(comparator_2_eq));  // open: gt, lt
  Comparator #(.width(3)) comparator_3 (.a(3'b010), .b(INSTRUCTION[14:12]), .eq(comparator_3_eq));  // open: gt, lt
  Multiplexer #(.enable("false"), .select(2), .width(4)) multiplexer_6 (
    .in1(priority_encoder_1_out), .in2(priority_encoder_2_out), .in3(priority_encoder_3_out),
    .out(multiplexer_6_out), .sel(priority_encoder_4_out));  // open: in0
  Priority_Encoder #(.select(2)) priority_encoder_4 (
    .in1(comparator_1_eq), .in2(comparator_2_eq), .in3(comparator_3_eq), .out(priority_encoder_4_out));  // open: in0, gs, en_out, en_in
  assign bit_extender_1_out = {{24{MEM_READ_DATA[7]}}, MEM_READ_DATA[7:0]};  // Bit_Extender bit_extender_1
  assign bit_extender_2_out = {{24{MEM_READ_DATA[15]}}, MEM_READ_DATA[15:8]};  // Bit_Extender bit_extender_2
  assign bit_extender_3_out = {{24{MEM_READ_DATA[23]}}, MEM_READ_DATA[23:16]};  // Bit_Extender bit_extender_3
  assign bit_extender_4_out = {{24{MEM_READ_DATA[31]}}, MEM_READ_DATA[31:24]};  // Bit_Extender bit_extender_4
  Multiplexer #(.enable("false"), .width(4)) multiplexer_7 (
    .in0(4'b0000), .in1(multiplexer_6_out), .out(MEM_WRITE_ENABLE), .sel(and_7_out));
  assign bit_extender_5_out = {{16{MEM_READ_DATA[15]}}, MEM_READ_DATA[15:0]};  // Bit_Extender bit_extender_5
  and and_7 (and_7_out, comparator_4_eq, memRw);
  Comparator #(.width(7)) comparator_4 (.a(7'b0100011), .b(INSTRUCTION[6:0]), .eq(comparator_4_eq));  // open: gt, lt
  assign bit_extender_6_out = {{16{MEM_READ_DATA[31]}}, MEM_READ_DATA[31:16]};  // Bit_Extender bit_extender_6
  Multiplexer #(.enable("false"), .select(4), .width(32)) multiplexer_8 (
    .in0({32{1'b0}}), .in1(bit_extender_1_out), .in2(bit_extender_2_out), .in3(bit_extender_5_out),
    .in4(bit_extender_3_out), .in8(bit_extender_4_out), .in12(bit_extender_6_out), .in15(MEM_READ_DATA),
    .out(multiplexer_8_out), .sel(multiplexer_6_out));  // open: in5, in6, in7, in9, in10, in11, in13, in14
  Multiplexer #(.enable("false"), .select(4), .width(32)) multiplexer_9 (
    .in0({32{1'b0}}), .in1({{24{1'b0}}, DATA_FROM_READ_DATA_2[7:0]}),
    .in2({{16{1'b0}}, DATA_FROM_READ_DATA_2[7:0], {8{1'b0}}}),
    .in3({{16{1'b0}}, DATA_FROM_READ_DATA_2[15:0]}),
    .in4({{8{1'b0}}, DATA_FROM_READ_DATA_2[7:0], {16{1'b0}}}),
    .in8({DATA_FROM_READ_DATA_2[7:0], {24{1'b0}}}), .in12({DATA_FROM_READ_DATA_2[15:0], {16{1'b0}}}),
    .in15(DATA_FROM_READ_DATA_2), .out(MEM_WRITE_DATA), .sel(multiplexer_6_out));  // open: in5, in6, in7, in9, in10, in11, in13, in14
  Comparator #(.width(7)) comparator_5 (.a(7'b0000011), .b(INSTRUCTION[6:0]), .eq(comparator_5_eq));  // open: gt, lt
  Multiplexer #(.enable("false"), .width(32)) multiplexer_10 (
    .in0({32{1'b0}}), .in1(multiplexer_8_out), .out(DATA_TO_READ), .sel(comparator_5_eq));

  // Other names for the same wires on the sheet: ALUout[31:0] = MEM_WRITE_ADDRESS

  // Notes on the sheet:
  //   Output to IMEM
  //   IMEM (do **NOT** move this)
  //   Inputs from IMEM
  //   It is OK to move the PC, RegFile, ALU, MEM, Branch Comp, Imm Gen, and Control Logic to wherever is most convenient for you when constructing your CPU, and to delete this text
  //   Inputs/Outputs for testing. Do **NOT** move these.
  //   Write_En generator for store
  //   Outputs To DMEM
  //   DMEM (do **NOT** move this)
  //   Inputs From DMEM
  //   LOAD PART OF WORD
  //   Load word (read_data_selector)
endmodule
