// Logisim project cpu-myTest.circ as structural Verilog: 1 circuit, main circuit run_main
module run_main (
  output [31:0] ra,
  output [31:0] sp,
  output [31:0] t0,
  output [31:0] t1,
  output [31:0] t2,
  output [31:0] s0,
  output [31:0] s1,
  output [31:0] a0,
  output [31:0] Requested_Address,
  output [31:0] Requested_Instruction,
  output [15:0] Time_Step,
  output halt
);

  wire clk;

  Clock clock_1 (.out(clk));
  // Probe on Requested_Address
  // cpu_harness cpu_harness_1: pin names not known; wires that end beside it: Requested_Instruction, clk, Requested_Address, ra, sp, t0, t1, t2, s0, s1, a0
  ROM #(.addrWidth(14), .dataWidth(32)) rom_1 (.addr(Requested_Address[15:2]), .data(Requested_Instruction));
  // Probe on Requested_Instruction
  Counter #(.max('hffff), .width(16)) counter_1 (.clk(clk), .Q(Time_Step));  // open: clr, load, up, count, D, carry
  Comparator #(.width(16)) comparator_1 (.a(Time_Step), .b(16'h9a), .eq(halt));  // open: gt, lt

  // Other names for the same wires on the sheet: INSTRUCTION[31:0] = Requested_Instruction;
  //   PROGRAM_COUNTER[31:0] = Requested_Address

  // Notes on the sheet:
  //   contents of rom_1 (hex, n*v repeats v):
  //   400293 500313 28393 E13 28293 228293 128293 429293 42D293 4022D293 32A293 C28293 1034293 F28293
  //   E2D293 1728293 40735293 628293 22E293 228293 52F293 628293 737293 5282B3 406282B3 E00293 40530333
  //   630333 530333 730333 1400293 1600313 26282B3 6292B3 26292B3 1400293 1400313 262B2B3 62A2B3 6400293
  //   5342B3 6400313 5352B3 405352B3 5362B3 63E333 637333 313 100293 130313 FE530EE3 313 393 500293 130313
  //   FE531EE3 313 393 500293 130313 FE534EE3 313 393 500293 130313 FE62DEE3 313 393 500293 130313
  //   FE536EE3 313 393 500293 130313 FE62FEE3 400313 7D000393 638023 6380A3 638123 6381A3 638223
  //   Instruction Memory
  //   Halts Execution After Constant # of Clock Cycles
  //   Constant
endmodule
